// Logisim project KeyboardInputAWSD.circ as structural Verilog: 1 circuit, main circuit main
module main (
  input  [6:0] Keyboard_out,
  input  Keyboard_rst,
  output out_3,
  output Down_pressed,
  output Left_pressed,
  output Right_pressed
);

  or or_1 (Keyboard_rst, out_3, Down_pressed, Left_pressed, Right_pressed);
  DotMatrix #(.matrixcols(1), .matrixrows(1), .persist(2048)) dotmatrix_1 (.col0(out_3));
  Comparator #(.width(7), .mode("unsigned")) comparator_1 (
    .a(7'b1110111), .b(Keyboard_out), .eq(out_3));  // open: gt, lt
  DotMatrix #(.matrixcols(1), .matrixrows(1), .persist(2048)) dotmatrix_2 (.col0(Down_pressed));
  Comparator #(.width(7), .mode("unsigned")) comparator_2 (
    .a(7'b1110011), .b(Keyboard_out), .eq(Down_pressed));  // open: gt, lt
  DotMatrix #(.matrixcols(1), .matrixrows(1), .persist(2048)) dotmatrix_3 (.col0(Left_pressed));
  Comparator #(.width(7), .mode("unsigned")) comparator_3 (
    .a(7'b1100001), .b(Keyboard_out), .eq(Left_pressed));  // open: gt, lt
  DotMatrix #(.matrixcols(1), .matrixrows(1), .persist(2048)) dotmatrix_4 (.col0(Right_pressed));
  Comparator #(.width(7), .mode("unsigned")) comparator_4 (
    .a(7'b1100100), .b(Keyboard_out), .eq(Right_pressed));  // open: gt, lt

  // Notes on the sheet:
  //   Up (W)
  //   Down (S)
  //   Left (A)
  //   Right (D)
  //   Tak, to dziala.
  //   Up pressed
endmodule
