// Logisim project app.circ as structural Verilog: 1 circuit, main circuit main
module main (
  input  HUMAN,
  input  in_2,
  input  [6:0] in_3,
  input  in_4,
  input  [6:0] in_5,
  output [4:0] out_6,
  output [4:0] out_7,
  output [4:0] out_8,
  output [4:0] out_9,
  output [4:0] out_10,
  output [4:0] out_11,
  output [4:0] out_12,
  output [4:0] out_13,
  output out_14,
  output out_15,
  output [29:0] out_16,
  output [29:0] out_17,
  output [29:0] out_18,
  output [29:0] out_19,
  output [29:0] out_20,
  output [29:0] out_21,
  output [29:0] out_22,
  output [29:0] out_23,
  output [29:0] out_24,
  output [29:0] out_25,
  output [29:0] out_26,
  output [29:0] out_27,
  output [29:0] out_28,
  output [29:0] out_29,
  output [29:0] out_30,
  output [29:0] out_31,
  output [29:0] out_32,
  output [29:0] out_33,
  output [29:0] out_34,
  output [29:0] out_35,
  output [29:0] out_36,
  output [29:0] out_37,
  output [29:0] out_38,
  output [29:0] out_39,
  output [29:0] out_40,
  output [29:0] out_41,
  output [29:0] out_42,
  output [29:0] out_43,
  output [29:0] out_44,
  output [29:0] out_45,
  output [29:0] out_46,
  output [29:0] out_47,
  output [29:0] out_48,
  output [29:0] out_49,
  output [29:0] out_50,
  output [29:0] out_51,
  output [29:0] out_52,
  output [29:0] out_53,
  output [29:0] out_54,
  output [29:0] out_55,
  output [29:0] out_56,
  output [29:0] out_57,
  output [29:0] out_58,
  output [29:0] out_59,
  output [29:0] out_60,
  output [29:0] out_61,
  output [29:0] out_62,
  output [29:0] out_63,
  output [29:0] out_64,
  output [29:0] out_65,
  output [29:0] out_66,
  output [29:0] out_67,
  output [29:0] out_68,
  output [29:0] out_69,
  output [29:0] out_70,
  output [29:0] out_71,
  output [29:0] out_72,
  output [29:0] out_73,
  output [29:0] out_74,
  output [29:0] out_75,
  output [29:0] out_76,
  output [29:0] out_77,
  output [29:0] out_78,
  output [29:0] out_79,
  output [29:0] out_80,
  output [29:0] out_81,
  output [29:0] out_82,
  output [29:0] out_83,
  output [29:0] out_84,
  output [29:0] out_85,
  output [29:0] out_86,
  output [29:0] out_87,
  output [29:0] out_88,
  output [29:0] out_89,
  output [29:0] out_90,
  output [29:0] out_91,
  output [29:0] out_92,
  output [29:0] out_93,
  output [29:0] out_94,
  output [29:0] out_95,
  output [29:0] out_96,
  output [29:0] out_97,
  output [29:0] out_98,
  output [29:0] out_99,
  output [29:0] out_100,
  output [29:0] out_101,
  output [29:0] out_102,
  output [29:0] out_103,
  output [29:0] out_104,
  output [29:0] out_105,
  output [29:0] out_106,
  output [29:0] out_107,
  output [29:0] out_108,
  output [29:0] out_109,
  output [29:0] out_110,
  output [29:0] out_111,
  output [29:0] out_112,
  output [29:0] out_113,
  output [29:0] out_114,
  output [29:0] out_115,
  output [29:0] out_116,
  output [29:0] out_117,
  output [29:0] out_118,
  output [29:0] out_119,
  output [29:0] out_120,
  output [29:0] out_121,
  output [29:0] out_122,
  output [29:0] out_123,
  output [29:0] out_124,
  output [29:0] out_125,
  output [29:0] out_126,
  output [29:0] out_127,
  output [29:0] out_128,
  output [29:0] out_129,
  output [29:0] out_130,
  output [29:0] out_131,
  output [29:0] out_132,
  output [29:0] out_133,
  output [29:0] out_134,
  output [29:0] out_135,
  output [29:0] out_136,
  output [29:0] out_137,
  output [29:0] out_138,
  output [29:0] out_139,
  output [29:0] out_140,
  output [29:0] out_141,
  output [29:0] out_142,
  output [29:0] out_143,
  output [29:0] out_144,
  output [29:0] out_145,
  output [29:0] out_146,
  output [29:0] out_147,
  output [29:0] out_148,
  output [29:0] out_149,
  output [29:0] out_150,
  output [29:0] out_151,
  output [29:0] out_152,
  output [29:0] out_153,
  output [29:0] out_154,
  output [29:0] out_155,
  output [29:0] out_156,
  output [29:0] out_157,
  output [29:0] out_158,
  output [29:0] out_159,
  output [29:0] out_160,
  output [29:0] out_161,
  output [29:0] out_162,
  output [29:0] out_163,
  output [29:0] out_164,
  output [29:0] out_165,
  output [29:0] out_166,
  output [29:0] out_167,
  output [29:0] out_168,
  output [29:0] out_169,
  output [29:0] out_170,
  output [29:0] out_171,
  output [29:0] out_172,
  output [29:0] out_173,
  output [29:0] out_174,
  output [29:0] out_175,
  output [29:0] out_176,
  output [29:0] out_177,
  output [29:0] out_178,
  output [29:0] out_179,
  output [29:0] out_180,
  output [29:0] out_181,
  output [29:0] out_182,
  output [29:0] out_183,
  output [29:0] out_184,
  output [29:0] out_185,
  output [29:0] out_186,
  output [29:0] out_187,
  output [29:0] out_188,
  output [29:0] out_189,
  output [29:0] out_190,
  output [29:0] out_191,
  output [29:0] out_192,
  output [29:0] out_193,
  output [29:0] out_194,
  output [29:0] out_195,
  output [29:0] out_196,
  output [29:0] out_197,
  output [29:0] out_198,
  output [29:0] out_199,
  output [29:0] out_200,
  output [29:0] out_201,
  output [29:0] out_202,
  output [29:0] out_203,
  output [29:0] out_204,
  output [29:0] out_205,
  output [29:0] out_206,
  output [29:0] out_207,
  output [29:0] out_208,
  output [29:0] out_209,
  output [29:0] out_210,
  output [29:0] out_211,
  output [29:0] out_212,
  output [29:0] out_213,
  output [29:0] out_214,
  output [29:0] out_215,
  output [29:0] out_216,
  output [29:0] out_217,
  output [29:0] out_218,
  output [29:0] out_219,
  output [29:0] out_220,
  output [29:0] out_221,
  output [29:0] out_222,
  output [29:0] out_223,
  output [29:0] out_224,
  output [29:0] out_225,
  output [29:0] out_226,
  output [29:0] out_227,
  output [29:0] out_228,
  output [29:0] out_229,
  output [29:0] out_230,
  output [29:0] out_231,
  output [29:0] out_232,
  output [29:0] out_233,
  output [29:0] out_234,
  output [29:0] out_235,
  output [29:0] out_236,
  output [29:0] out_237,
  output [29:0] out_238,
  output [29:0] out_239,
  output [29:0] out_240,
  output [29:0] out_241,
  output [29:0] out_242,
  output [29:0] out_243,
  output [29:0] out_244,
  output [29:0] out_245,
  output [29:0] out_246,
  output [29:0] out_247,
  output [29:0] out_248,
  output [29:0] out_249,
  output [29:0] out_250,
  output [29:0] out_251,
  output [29:0] out_252,
  output [29:0] out_253,
  output [29:0] out_254,
  output [29:0] out_255,
  output [29:0] out_256,
  output [29:0] out_257,
  output [29:0] out_258,
  output [29:0] out_259,
  output [29:0] out_260,
  output [29:0] out_261,
  output [29:0] out_262,
  output [29:0] out_263,
  output [29:0] out_264,
  output [29:0] out_265,
  output [29:0] out_266,
  output [29:0] out_267,
  output [29:0] out_268,
  output [29:0] out_269,
  output [29:0] out_270,
  output [29:0] out_271,
  output [29:0] out_272,
  output [29:0] out_273,
  output [29:0] out_274,
  output [29:0] out_275,
  output [29:0] out_276,
  output [29:0] out_277,
  output [29:0] out_278,
  output [29:0] out_279,
  output [29:0] out_280,
  output [29:0] out_281,
  output [29:0] out_282,
  output [29:0] out_283,
  output [29:0] out_284,
  output [29:0] out_285,
  output [29:0] out_286,
  output [29:0] out_287,
  output [29:0] out_288,
  output [29:0] out_289,
  output [29:0] out_290,
  output [29:0] out_291,
  output [29:0] out_292,
  output [29:0] out_293,
  output [29:0] out_294,
  output [29:0] out_295,
  output [29:0] out_296,
  output [29:0] out_297,
  output [29:0] out_298,
  output [29:0] out_299,
  output [29:0] out_300,
  output [29:0] out_301,
  output [29:0] out_302,
  output [29:0] out_303,
  output [29:0] out_304,
  output [29:0] out_305,
  output [29:0] out_306,
  output [29:0] out_307,
  output [29:0] out_308,
  output [29:0] out_309,
  output [29:0] out_310,
  output [29:0] out_311,
  output [29:0] out_312,
  output [29:0] out_313,
  output [29:0] out_314,
  output [29:0] out_315,
  output [29:0] out_316,
  output [29:0] out_317,
  output [29:0] out_318,
  output [29:0] out_319,
  output [29:0] out_320,
  output [29:0] out_321,
  output [29:0] out_322,
  output [29:0] out_323,
  output [29:0] out_324,
  output [29:0] out_325,
  output [29:0] out_326,
  output [29:0] out_327,
  output [29:0] out_328,
  output [29:0] out_329,
  output [29:0] out_330,
  output [29:0] out_331,
  output [29:0] out_332,
  output [29:0] out_333,
  output [29:0] out_334,
  output [29:0] out_335,
  output [29:0] out_336,
  output [29:0] out_337,
  output [29:0] out_338,
  output [29:0] out_339,
  output [29:0] out_340,
  output [29:0] out_341,
  output [29:0] out_342,
  output [29:0] out_343,
  output [29:0] out_344,
  output [29:0] out_345,
  output [29:0] out_346,
  output [29:0] out_347,
  output [29:0] out_348,
  output [29:0] out_349,
  output [29:0] out_350,
  output [29:0] out_351,
  output [29:0] out_352,
  output [29:0] out_353,
  output [29:0] out_354,
  output [29:0] out_355,
  output [29:0] out_356,
  output [29:0] out_357,
  output [29:0] out_358,
  output [29:0] out_359,
  output [29:0] out_360,
  output [29:0] out_361,
  output [29:0] out_362,
  output [29:0] out_363,
  output [29:0] out_364,
  output [29:0] out_365,
  output [29:0] out_366,
  output [29:0] out_367,
  output [29:0] out_368,
  output [29:0] out_369,
  output [29:0] out_370,
  output [29:0] out_371,
  output [29:0] out_372,
  output [29:0] out_373,
  output [29:0] out_374,
  output [29:0] out_375,
  output [29:0] out_376,
  output [29:0] out_377,
  output [29:0] out_378,
  output [29:0] out_379,
  output [29:0] out_380,
  output [29:0] out_381,
  output [29:0] out_382,
  output [29:0] out_383,
  output [29:0] out_384,
  output [29:0] out_385,
  output [29:0] out_386,
  output [29:0] out_387,
  output [29:0] out_388,
  output [29:0] out_389,
  output [29:0] out_390,
  output [29:0] out_391,
  output [29:0] out_392,
  output [29:0] out_393,
  output [29:0] out_394,
  output [29:0] out_395,
  output [29:0] out_396,
  output [29:0] out_397,
  output [29:0] out_398,
  output [29:0] out_399,
  output [29:0] out_400,
  output [29:0] out_401,
  output [29:0] out_402,
  output [29:0] out_403,
  output [29:0] out_404,
  output [29:0] out_405,
  output [29:0] out_406,
  output [29:0] out_407,
  output [29:0] out_408,
  output [29:0] out_409,
  output [29:0] out_410,
  output [29:0] out_411,
  output [29:0] out_412,
  output [29:0] out_413,
  output [29:0] out_414,
  output [29:0] out_415,
  output [29:0] out_416,
  output [29:0] out_417,
  output [29:0] out_418,
  output [29:0] out_419,
  output [29:0] out_420,
  output [29:0] out_421,
  output [29:0] out_422,
  output [29:0] out_423,
  output [29:0] out_424,
  output [29:0] out_425,
  output [29:0] out_426,
  output [29:0] out_427,
  output [29:0] out_428,
  output [29:0] out_429,
  output [29:0] out_430,
  output [29:0] out_431,
  output [29:0] out_432,
  output [29:0] out_433,
  output [29:0] out_434,
  output [29:0] out_435,
  output [29:0] out_436,
  output [29:0] out_437,
  output [29:0] out_438,
  output [29:0] out_439,
  output [29:0] out_440,
  output [29:0] out_441,
  output [29:0] out_442,
  output [29:0] out_443,
  output [29:0] out_444,
  output [29:0] out_445,
  output [29:0] out_446,
  output [29:0] out_447,
  output [29:0] out_448,
  output [29:0] out_449,
  output [29:0] out_450,
  output [29:0] out_451,
  output [29:0] out_452,
  output [29:0] out_453,
  output [29:0] out_454,
  output [29:0] out_455,
  output [29:0] out_456,
  output [29:0] out_457,
  output [29:0] out_458,
  output [29:0] out_459,
  output [29:0] out_460,
  output [29:0] out_461,
  output [29:0] out_462,
  output [29:0] out_463,
  output [29:0] out_464,
  output [29:0] out_465,
  output [29:0] out_466,
  output [29:0] out_467,
  output [29:0] out_468,
  output [29:0] out_469,
  output [29:0] out_470,
  output [29:0] out_471,
  output [29:0] out_472,
  output [29:0] out_473,
  output [29:0] out_474,
  output [29:0] out_475,
  output [29:0] out_476,
  output [29:0] out_477,
  output [29:0] out_478,
  output [29:0] out_479,
  output [29:0] out_480,
  output [29:0] out_481,
  output [29:0] out_482,
  output [29:0] out_483,
  output [29:0] out_484,
  output [29:0] out_485,
  output [29:0] out_486,
  output [29:0] out_487,
  output [29:0] out_488,
  output [29:0] out_489,
  output [29:0] out_490,
  output [29:0] out_491,
  output [29:0] out_492,
  output [29:0] out_493,
  output [29:0] out_494,
  output [29:0] out_495
);

  wire and_1_out, and_2_out, and_3_out, and_5_out, and_6_out, and_7_out, and_8_out, and_11_out, and_12_out,
       and_13_out, and_14_out, and_15_out, and_16_out, and_17_out, and_18_out, and_19_out, and_20_out,
       and_23_out, and_24_out, CLK_5, comparator_1_eq, comparator_2_eq, comparator_3_gt, comparator_4_gt,
       comparator_5_eq, comparator_5_lt, comparator_6_gt, comparator_7_gt, comparator_8_eq, comparator_8_lt,
       CURR_PLAYER, main_2_confirm, main_29_confirm, main_29_rotated, main_30_confirm, main_30_rotated,
       not_1_out, not_2_out, not_3_out, not_4_out, not_5_out, not_6_out, not_7_out, not_8_out, not_9_out,
       or_3_out, or_5_out, P1_ADD_SHIP, P1_CHECK_SHIP, P1_CHECKING, P1_CONF, P1_CURR_SEG_ALIVE, P1_DOT_ADDED,
       P1_HIT, P1_NEXT_SHIP, P1_RO_ROTATED, P1_ROTATED, P1_SHIP_DRAW_ENABLE, P1_WIN, P2_ADD_SHIP,
       P2_CHECK_SHIP, P2_CHECKING, P2_CONF, P2_CURR_SEG_ALIVE, P2_DOT_ADDED, P2_HIT, P2_NEXT_SHIP,
       P2_RO_ROTATED, P2_ROTATED, P2_SHIP_DRAW_ENABLE, P2_WIN, PREP_PHASE_END;
  wire [1:0] P1_RO_SHIP_TYPE, P1_SEG_SEL, P2_RO_SHIP_TYPE, P2_SEG_SEL;
  wire [2:0] P1_SHIP_DRAW_ON_ENEMY_SEL, P1_SHIP_DRAW_SEL, P2_SHIP_DRAW_ON_ENEMY_SEL, P2_SHIP_DRAW_SEL;
  wire [3:0] main_29_cur_x, main_29_cur_y, main_30_x, main_30_y, P1_CUR_X, P1_CUR_Y, P1_CURR_SHIP_ADD,
       P1_RO_ALIVE, P1_RO_SHIP_X, P1_RO_SHIP_Y, P2_CUR_X, P2_CUR_Y, P2_CURR_SHIP_ADD, P2_RO_ALIVE,
       P2_RO_SHIP_X, P2_RO_SHIP_Y;
  wire [4:0] main_29_bl_sel, main_29_br_sel, main_29_tl_sel, main_29_tr_sel, P1_CUR_BL_SEL, P1_CUR_BR_SEL,
       P1_CUR_TL_SEL, P1_CUR_TR_SEL, P1_DOT_BL_SEL, P1_DOT_BR_SEL, P1_DOT_TL_SEL, P1_DOT_TR_SEL,
       P1_SHIP_BL_SEL, P1_SHIP_BR_SEL, P1_SHIP_ON_EN_BL_SEL, P1_SHIP_ON_EN_BR_SEL, P1_SHIP_ON_EN_TL_SEL,
       P1_SHIP_ON_EN_TR_SEL, P1_SHIP_TL_SEL, P1_SHIP_TR_SEL, P2_CUR_BL_SEL, P2_CUR_BR_SEL, P2_CUR_TL_SEL,
       P2_CUR_TR_SEL, P2_DOT_BL_SEL, P2_DOT_BR_SEL, P2_DOT_TL_SEL, P2_DOT_TR_SEL, P2_SHIP_BL_SEL,
       P2_SHIP_BR_SEL, P2_SHIP_ON_EN_BL_SEL, P2_SHIP_ON_EN_BR_SEL, P2_SHIP_ON_EN_TL_SEL,
       P2_SHIP_ON_EN_TR_SEL, P2_SHIP_TL_SEL, P2_SHIP_TR_SEL;
  wire [5:0] main_12_out_x_00, main_12_out_x_01, main_12_out_x_10, main_12_out_x_11, main_12_out_y_00,
       main_12_out_y_01, main_12_out_y_10, main_12_out_y_11, main_26_out_x_00, main_26_out_x_01,
       main_26_out_x_10, main_26_out_x_11, main_26_out_y_00, main_26_out_y_01, main_26_out_y_10,
       main_26_out_y_11, P1_SHIP_SCR_X, P1_SHIP_SCR_Y, P2_SHIP_SCR_X, P2_SHIP_SCR_Y;
  wire [29:0] controlled_buffer_1_out, controlled_buffer_2_out, controlled_buffer_3_out,
       controlled_buffer_4_out, controlled_buffer_5_out, controlled_buffer_6_out, controlled_buffer_7_out,
       controlled_buffer_8_out, controlled_buffer_9_out, controlled_buffer_10_out, controlled_buffer_11_out,
       controlled_buffer_12_out, controlled_buffer_13_out, controlled_buffer_14_out,
       controlled_buffer_15_out, controlled_buffer_16_out, main_29_bl_data, main_29_br_data, main_29_tl_data,
       main_29_tr_data, P1_CUR_BL_DATA, P1_CUR_BR_DATA, P1_CUR_TL_DATA, P1_CUR_TR_DATA, P1_DOT_BL_DATA,
       P1_DOT_BR_DATA, P1_DOT_TL_DATA, P1_DOT_TR_DATA, P1_SHIP_BL_DATA, P1_SHIP_BR_DATA,
       P1_SHIP_ON_EN_BL_DATA, P1_SHIP_ON_EN_BR_DATA, P1_SHIP_ON_EN_TL_DATA, P1_SHIP_ON_EN_TR_DATA,
       P1_SHIP_TL_DATA, P1_SHIP_TR_DATA, P2_CUR_BL_DATA, P2_CUR_BR_DATA, P2_CUR_TL_DATA, P2_CUR_TR_DATA,
       P2_DOT_BL_DATA, P2_DOT_BR_DATA, P2_DOT_TL_DATA, P2_DOT_TR_DATA, P2_SHIP_BL_DATA, P2_SHIP_BR_DATA,
       P2_SHIP_ON_EN_BL_DATA, P2_SHIP_ON_EN_BR_DATA, P2_SHIP_ON_EN_TL_DATA, P2_SHIP_ON_EN_TR_DATA,
       P2_SHIP_TL_DATA, P2_SHIP_TR_DATA;

  Clock clock_1 (.out(out_14));
  Counter #(.width(3), .max('h4)) counter_1 (.carry(CLK_5), .clk(out_14));  // open: load, D, count, Q, clr
  Counter #(.width(2), .max('h3)) counter_2 (
    .Q(P1_SEG_SEL), .carry(P1_NEXT_SHIP), .clk(CLK_5));  // open: load, D, count, clr
  memory_management_main main_1 (
    .X(P1_CUR_X), .Y(P1_CUR_Y), .ROTATED(P1_ROTATED),
    .RAM_OUT({P1_RO_ALIVE, P1_RO_ROTATED, P1_RO_SHIP_TYPE, P1_RO_SHIP_Y, P1_RO_SHIP_X}), .CHECK_X(P2_CUR_X),
    .CHECK_Y(P2_CUR_Y), .SINK_IF_HIT(1'b1), .CONFIRM(P1_ADD_SHIP), .CHECK(P2_CHECK_SHIP), .CLK(out_14),
    .SHOW_NEXT_SHIP(P1_NEXT_SHIP), .WIN(P1_WIN), .HIT(P1_HIT), .CHECKING(P1_CHECKING),
    .CURR_SHIP_ADD(P1_CURR_SHIP_ADD));  // open: in_2
  cursor_module_main main_2 (
    .CUR_X(P1_CUR_X), .CLK(out_14), .KEYBOARD_OUT(in_3), .KEYBOARD_RST(in_2), .TL_SEL(P1_CUR_TL_SEL),
    .TR_SEL(P1_CUR_TR_SEL), .BL_SEL(P1_CUR_BL_SEL), .BR_SEL(P1_CUR_BR_SEL), .TL_DATA(P1_CUR_TL_DATA),
    .TR_DATA(P1_CUR_TR_DATA), .BL_DATA(P1_CUR_BL_DATA), .BR_DATA(P1_CUR_BR_DATA), .CONFIRM(main_2_confirm),
    .CUR_Y(P1_CUR_Y), .ROTATED(P1_ROTATED));
  and and_1 (and_1_out, ~P1_HIT, ~P1_CHECKING, PREP_PHASE_END);  // AND_Gate
  demuxor_30x30x3_main main_3 (
    .DATA_1(P1_SHIP_TL_DATA), .SELECT_1(P1_SHIP_TL_SEL), .SELECT_2(P2_DOT_TL_SEL), .DATA_2(P2_DOT_TL_DATA),
    .SELECT_0(P1_CUR_TL_SEL), .DATA_0(controlled_buffer_1_out), .OUT_0(out_132), .OUT_1(out_128),
    .OUT_2(out_124), .OUT_3(out_120), .OUT_4(out_116), .OUT_6(out_108), .OUT_7(out_104), .OUT_8(out_100),
    .OUT_9(out_96), .OUT_a(out_92), .OUT_c(out_84), .OUT_12(out_60), .OUT_d(out_80), .OUT_13(out_56),
    .OUT_e(out_76), .OUT_14(out_52), .OUT_f(out_72), .OUT_15(out_48), .OUT_10(out_68), .OUT_16(out_44),
    .OUT_18(out_36), .OUT_19(out_32), .OUT_1a(out_28), .OUT_1b(out_24), .OUT_1c(out_20), .OUT_5(out_112),
    .OUT_b(out_88), .OUT_11(out_64), .OUT_17(out_40), .OUT_1d(out_16));
  assign controlled_buffer_1_out = not_1_out ? P1_CUR_TL_DATA : 30'bz;  // Controlled_Buffer controlled_buffer_1
  not not_1 (not_1_out, PREP_PHASE_END);
  demuxor_30x30x3_main main_4 (
    .DATA_1(P1_SHIP_BL_DATA), .SELECT_1(P1_SHIP_BL_SEL), .SELECT_2(P2_DOT_BL_SEL), .DATA_2(P2_DOT_BL_DATA),
    .SELECT_0(P1_CUR_BL_SEL), .DATA_0(controlled_buffer_2_out), .OUT_0(out_254), .OUT_1(out_250),
    .OUT_2(out_246), .OUT_3(out_242), .OUT_4(out_238), .OUT_6(out_230), .OUT_7(out_226), .OUT_8(out_222),
    .OUT_9(out_218), .OUT_a(out_214), .OUT_c(out_206), .OUT_12(out_182), .OUT_d(out_202), .OUT_13(out_178),
    .OUT_e(out_198), .OUT_14(out_174), .OUT_f(out_194), .OUT_15(out_170), .OUT_10(out_190), .OUT_16(out_166),
    .OUT_18(out_158), .OUT_19(out_154), .OUT_1a(out_150), .OUT_1b(out_146), .OUT_1c(out_142),
    .OUT_5(out_234), .OUT_b(out_210), .OUT_11(out_186), .OUT_17(out_162), .OUT_1d(out_138));
  assign controlled_buffer_2_out = not_2_out ? P1_CUR_BL_DATA : 30'bz;  // Controlled_Buffer controlled_buffer_2
  not not_2 (not_2_out, PREP_PHASE_END);
  demuxor_30x30x3_main main_5 (
    .DATA_1(P2_SHIP_ON_EN_TL_DATA), .SELECT_1(P2_SHIP_ON_EN_TL_SEL), .SELECT_2(P1_DOT_TL_SEL),
    .DATA_2(P1_DOT_TL_DATA), .SELECT_0(P1_CUR_TL_SEL), .DATA_0(controlled_buffer_3_out), .OUT_0(out_374),
    .OUT_1(out_370), .OUT_2(out_366), .OUT_3(out_362), .OUT_4(out_358), .OUT_6(out_350), .OUT_7(out_346),
    .OUT_8(out_342), .OUT_9(out_338), .OUT_a(out_334), .OUT_c(out_326), .OUT_12(out_302), .OUT_d(out_322),
    .OUT_13(out_298), .OUT_e(out_318), .OUT_14(out_294), .OUT_f(out_314), .OUT_15(out_290), .OUT_10(out_310),
    .OUT_16(out_286), .OUT_18(out_278), .OUT_19(out_274), .OUT_1a(out_270), .OUT_1b(out_266),
    .OUT_1c(out_262), .OUT_5(out_354), .OUT_b(out_330), .OUT_11(out_306), .OUT_17(out_282), .OUT_1d(out_258));
  assign controlled_buffer_3_out = and_2_out ? P1_CUR_TL_DATA : 30'bz;  // Controlled_Buffer controlled_buffer_3
  and and_2 (and_2_out, PREP_PHASE_END, ~CURR_PLAYER);  // AND_Gate
  demuxor_30x30x3_main main_6 (
    .DATA_1(P2_SHIP_ON_EN_BL_DATA), .SELECT_1(P2_SHIP_ON_EN_BL_SEL), .SELECT_2(P1_DOT_BL_SEL),
    .DATA_2(P1_DOT_BL_DATA), .SELECT_0(P1_CUR_BL_SEL), .DATA_0(controlled_buffer_4_out), .OUT_0(out_494),
    .OUT_1(out_490), .OUT_2(out_486), .OUT_3(out_482), .OUT_4(out_478), .OUT_6(out_470), .OUT_7(out_466),
    .OUT_8(out_462), .OUT_9(out_458), .OUT_a(out_454), .OUT_c(out_446), .OUT_12(out_422), .OUT_d(out_442),
    .OUT_13(out_418), .OUT_e(out_438), .OUT_14(out_414), .OUT_f(out_434), .OUT_15(out_410), .OUT_10(out_430),
    .OUT_16(out_406), .OUT_18(out_398), .OUT_19(out_394), .OUT_1a(out_390), .OUT_1b(out_386),
    .OUT_1c(out_382), .OUT_5(out_474), .OUT_b(out_450), .OUT_11(out_426), .OUT_17(out_402), .OUT_1d(out_378));
  assign controlled_buffer_4_out = and_3_out ? P1_CUR_BL_DATA : 30'bz;  // Controlled_Buffer controlled_buffer_4
  and and_3 (and_3_out, PREP_PHASE_END, ~CURR_PLAYER);  // AND_Gate
  not_hit_module_main main_7 (
    .nHIT_X(P2_CUR_X), .nHIT_Y(P2_CUR_Y), .nHIT(and_1_out), .CLK(out_14), .TL_DATA(P2_DOT_TL_DATA),
    .TR_DATA(P2_DOT_TR_DATA), .BL_DATA(P2_DOT_BL_DATA), .BR_DATA(P2_DOT_BR_DATA), .TL_SEL(P2_DOT_TL_SEL),
    .TR_SEL(P2_DOT_TR_SEL), .BL_SEL(P2_DOT_BL_SEL), .BR_SEL(P2_DOT_BR_SEL), .ADDED(P1_DOT_ADDED));
  Comparator #(.width(4), .mode("unsigned")) comparator_1 (
    .a(P1_CURR_SHIP_ADD), .b(4'b1010), .eq(comparator_1_eq));  // open: gt, lt
  Comparator #(.width(4), .mode("unsigned")) comparator_2 (
    .a(4'b1010), .b(P2_CURR_SHIP_ADD), .eq(comparator_2_eq));  // open: gt, lt
  Multiplexer #(.select(2), .enable("false")) multiplexer_1 (
    .in0(P1_RO_ALIVE[0]), .in1(P1_RO_ALIVE[1]), .in2(P1_RO_ALIVE[2]), .in3(P1_RO_ALIVE[3]),
    .out(P1_CURR_SEG_ALIVE), .sel(P1_SEG_SEL));
  and and_4 (PREP_PHASE_END, comparator_1_eq, comparator_2_eq);
  Multiplexer #(.width(3), .enable("false")) multiplexer_2 (
    .in0(3'b010), .in1(3'b001), .out(P1_SHIP_DRAW_SEL), .sel(P1_CURR_SEG_ALIVE));
  Multiplexer #(.width(3), .enable("false")) multiplexer_3 (
    .in0(3'b010), .in1(3'b100), .out(P1_SHIP_DRAW_ON_ENEMY_SEL), .sel(P1_CURR_SEG_ALIVE));
  and and_5 (and_5_out, ~PREP_PHASE_END, main_2_confirm);  // AND_Gate
  and and_6 (and_6_out, main_2_confirm, ~CURR_PLAYER);  // AND_Gate
  demuxor_30x30x3_main main_8 (
    .DATA_1(P1_SHIP_TR_DATA), .SELECT_1(P1_SHIP_TR_SEL), .SELECT_2(P2_DOT_TR_SEL), .DATA_2(P2_DOT_TR_DATA),
    .SELECT_0(P1_CUR_TR_SEL), .DATA_0(controlled_buffer_5_out), .OUT_0(out_133), .OUT_1(out_129),
    .OUT_2(out_125), .OUT_3(out_121), .OUT_4(out_117), .OUT_6(out_109), .OUT_7(out_105), .OUT_8(out_101),
    .OUT_9(out_97), .OUT_a(out_93), .OUT_c(out_85), .OUT_12(out_61), .OUT_d(out_81), .OUT_13(out_57),
    .OUT_e(out_77), .OUT_14(out_53), .OUT_f(out_73), .OUT_15(out_49), .OUT_10(out_69), .OUT_16(out_45),
    .OUT_18(out_37), .OUT_19(out_33), .OUT_1a(out_29), .OUT_1b(out_25), .OUT_1c(out_21), .OUT_5(out_113),
    .OUT_b(out_89), .OUT_11(out_65), .OUT_17(out_41), .OUT_1d(out_17));
  demuxor_30x30x3_main main_9 (
    .DATA_1(P1_SHIP_BR_DATA), .SELECT_1(P1_SHIP_BR_SEL), .SELECT_2(P2_DOT_BR_SEL), .DATA_2(P2_DOT_BR_DATA),
    .SELECT_0(P1_CUR_BR_SEL), .DATA_0(controlled_buffer_6_out), .OUT_0(out_255), .OUT_1(out_251),
    .OUT_2(out_247), .OUT_3(out_243), .OUT_4(out_239), .OUT_6(out_231), .OUT_7(out_227), .OUT_8(out_223),
    .OUT_9(out_219), .OUT_a(out_215), .OUT_c(out_207), .OUT_12(out_183), .OUT_d(out_203), .OUT_13(out_179),
    .OUT_e(out_199), .OUT_14(out_175), .OUT_f(out_195), .OUT_15(out_171), .OUT_10(out_191), .OUT_16(out_167),
    .OUT_18(out_159), .OUT_19(out_155), .OUT_1a(out_151), .OUT_1b(out_147), .OUT_1c(out_143),
    .OUT_5(out_235), .OUT_b(out_211), .OUT_11(out_187), .OUT_17(out_163), .OUT_1d(out_139));
  not not_3 (not_3_out, PREP_PHASE_END);
  demuxor_30x30x3_main main_10 (
    .DATA_1(P2_SHIP_ON_EN_TR_DATA), .SELECT_1(P2_SHIP_ON_EN_TR_SEL), .SELECT_2(P1_DOT_TR_SEL),
    .DATA_2(P1_DOT_TR_DATA), .SELECT_0(P1_CUR_TR_SEL), .DATA_0(controlled_buffer_7_out), .OUT_0(out_375),
    .OUT_1(out_371), .OUT_2(out_367), .OUT_3(out_363), .OUT_4(out_359), .OUT_6(out_351), .OUT_7(out_347),
    .OUT_8(out_343), .OUT_9(out_339), .OUT_a(out_335), .OUT_c(out_327), .OUT_12(out_303), .OUT_d(out_323),
    .OUT_13(out_299), .OUT_e(out_319), .OUT_14(out_295), .OUT_f(out_315), .OUT_15(out_291), .OUT_10(out_311),
    .OUT_16(out_287), .OUT_18(out_279), .OUT_19(out_275), .OUT_1a(out_271), .OUT_1b(out_267),
    .OUT_1c(out_263), .OUT_5(out_355), .OUT_b(out_331), .OUT_11(out_307), .OUT_17(out_283), .OUT_1d(out_259));
  and and_7 (and_7_out, PREP_PHASE_END, ~CURR_PLAYER);  // AND_Gate
  demuxor_30x30x3_main main_11 (
    .DATA_1(P2_SHIP_ON_EN_BR_DATA), .SELECT_1(P2_SHIP_ON_EN_BR_SEL), .SELECT_2(P1_DOT_BR_SEL),
    .DATA_2(P1_DOT_BR_DATA), .SELECT_0(P1_CUR_BR_SEL), .DATA_0(controlled_buffer_8_out), .OUT_0(out_495),
    .OUT_1(out_491), .OUT_2(out_487), .OUT_3(out_483), .OUT_4(out_479), .OUT_6(out_471), .OUT_7(out_467),
    .OUT_8(out_463), .OUT_9(out_459), .OUT_a(out_455), .OUT_c(out_447), .OUT_12(out_423), .OUT_d(out_443),
    .OUT_13(out_419), .OUT_e(out_439), .OUT_14(out_415), .OUT_f(out_435), .OUT_15(out_411), .OUT_10(out_431),
    .OUT_16(out_407), .OUT_18(out_399), .OUT_19(out_395), .OUT_1a(out_391), .OUT_1b(out_387),
    .OUT_1c(out_383), .OUT_5(out_475), .OUT_b(out_451), .OUT_11(out_427), .OUT_17(out_403), .OUT_1d(out_379));
  and and_8 (and_8_out, PREP_PHASE_END, ~CURR_PLAYER);  // AND_Gate
  or or_1 (P1_CONF, and_5_out, and_6_out);
  assign controlled_buffer_5_out = not_4_out ? P1_CUR_TR_DATA : 30'bz;  // Controlled_Buffer controlled_buffer_5
  not not_4 (not_4_out, PREP_PHASE_END);
  assign controlled_buffer_6_out = not_3_out ? P1_CUR_BR_DATA : 30'bz;  // Controlled_Buffer controlled_buffer_6
  assign controlled_buffer_7_out = and_7_out ? P1_CUR_TR_DATA : 30'bz;  // Controlled_Buffer controlled_buffer_7
  assign controlled_buffer_8_out = and_8_out ? P1_CUR_BR_DATA : 30'bz;  // Controlled_Buffer controlled_buffer_8
  and and_9 (P1_ADD_SHIP, P1_CONF, ~PREP_PHASE_END);  // AND_Gate
  and and_10 (P1_CHECK_SHIP, P1_CONF, PREP_PHASE_END);
  Comparator #(.width(4), .mode("unsigned")) comparator_3 (
    .a(P1_CURR_SHIP_ADD), .b(4'b0000), .gt(comparator_3_gt));  // open: eq, lt
  Comparator #(.width(4), .mode("unsigned")) comparator_4 (
    .a(P1_CURR_SHIP_ADD), .b(4'b0000), .gt(comparator_4_gt));  // open: eq, lt
  ship_xyr_to_screen_xy_main main_12 (
    .in_1(P1_RO_SHIP_X), .in_2(P1_RO_SHIP_Y), .in_3(P1_RO_ROTATED), .OUT_X_00(main_12_out_x_00),
    .OUT_Y_00(main_12_out_y_00), .OUT_X_01(main_12_out_x_01), .OUT_Y_01(main_12_out_y_01),
    .OUT_X_10(main_12_out_x_10), .OUT_Y_10(main_12_out_y_10), .OUT_X_11(main_12_out_x_11),
    .OUT_Y_11(main_12_out_y_11));
  screen_xy_to_screen_data_main main_13 (
    .SCREEN_X(P1_SHIP_SCR_X), .SCREEN_Y(P1_SHIP_SCR_Y), .DATA_TO_DISPLAY(P1_SHIP_DRAW_SEL),
    .TL_SEL_OUT(P1_SHIP_TL_SEL), .TR_SEL_OUT(P1_SHIP_TR_SEL), .BL_SEL_OUT(P1_SHIP_BL_SEL),
    .BR_SEL_OUT(P1_SHIP_BR_SEL), .TL_DATA_OUT(P1_SHIP_TL_DATA), .TR_DATA_OUT(P1_SHIP_TR_DATA),
    .BL_DATA_OUT(P1_SHIP_BL_DATA), .BR_DATA_OUT(P1_SHIP_BR_DATA), .CLK(out_14), .ENABLE(and_11_out));
  and and_11 (and_11_out, P1_SHIP_DRAW_ENABLE, comparator_3_gt);
  screen_xy_to_screen_data_main main_14 (
    .SCREEN_X(P1_SHIP_SCR_X), .SCREEN_Y(P1_SHIP_SCR_Y), .DATA_TO_DISPLAY(P1_SHIP_DRAW_ON_ENEMY_SEL),
    .TL_SEL_OUT(P1_SHIP_ON_EN_TL_SEL), .TR_SEL_OUT(P1_SHIP_ON_EN_TR_SEL), .BL_SEL_OUT(P1_SHIP_ON_EN_BL_SEL),
    .BR_SEL_OUT(P1_SHIP_ON_EN_BR_SEL), .TL_DATA_OUT(P1_SHIP_ON_EN_TL_DATA),
    .TR_DATA_OUT(P1_SHIP_ON_EN_TR_DATA), .BL_DATA_OUT(P1_SHIP_ON_EN_BL_DATA),
    .BR_DATA_OUT(P1_SHIP_ON_EN_BR_DATA), .CLK(out_14), .ENABLE(and_12_out));
  and and_12 (and_12_out, P1_SHIP_DRAW_ENABLE, comparator_4_gt);
  Comparator #(.width(2), .mode("unsigned")) comparator_5 (
    .a(P1_SEG_SEL), .b(P1_RO_SHIP_TYPE), .eq(comparator_5_eq), .lt(comparator_5_lt));  // open: gt
  or or_2 (P1_SHIP_DRAW_ENABLE, comparator_5_eq, comparator_5_lt);
  Multiplexer #(.select(2), .width(6), .enable("false")) multiplexer_4 (
    .in0(main_12_out_x_00), .in1(main_12_out_x_01), .in2(main_12_out_x_10), .in3(main_12_out_x_11),
    .out(P1_SHIP_SCR_X), .sel(P1_SEG_SEL));
  Multiplexer #(.select(2), .width(6), .enable("false")) multiplexer_5 (
    .in0(main_12_out_y_00), .in1(main_12_out_y_01), .in2(main_12_out_y_10), .in3(main_12_out_y_11),
    .out(P1_SHIP_SCR_Y), .sel(P1_SEG_SEL));
  or or_3 (or_3_out, P1_DOT_ADDED, P2_DOT_ADDED);
  Counter #(.width(1), .max('h1)) counter_3 (.Q(CURR_PLAYER), .clk(and_13_out));  // open: load, D, count, carry, clr
  and and_13 (and_13_out, ~P1_CHECKING, ~P2_CHECKING, ~P1_HIT, ~P2_HIT, or_3_out);  // AND_Gate
  arrow_main main_15 (
    .\input (CURR_PLAYER), .output2(out_7), .output1(out_6), .output3(out_8), .output4(out_9),
    .output5(out_10), .output6(out_11), .output7(out_12), .output8(out_13));
  Counter #(.width(2), .max('h3)) counter_4 (
    .Q(P2_SEG_SEL), .carry(P2_NEXT_SHIP), .clk(CLK_5));  // open: load, D, count, clr
  memory_management_main main_16 (
    .X(P2_CUR_X), .Y(P2_CUR_Y), .ROTATED(P2_ROTATED),
    .RAM_OUT({P2_RO_ALIVE, P2_RO_ROTATED, P2_RO_SHIP_TYPE, P2_RO_SHIP_Y, P2_RO_SHIP_X}), .CHECK_X(P1_CUR_X),
    .CHECK_Y(P1_CUR_Y), .SINK_IF_HIT(1'b1), .CONFIRM(P2_ADD_SHIP), .CHECK(P1_CHECK_SHIP), .CLK(out_14),
    .SHOW_NEXT_SHIP(P2_NEXT_SHIP), .WIN(P2_WIN), .HIT(P2_HIT), .CHECKING(P2_CHECKING),
    .CURR_SHIP_ADD(P2_CURR_SHIP_ADD));  // open: in_2
  and and_14 (and_14_out, ~P2_HIT, ~P2_CHECKING, PREP_PHASE_END);  // AND_Gate
  demuxor_30x30x3_main main_17 (
    .DATA_1(P2_SHIP_TL_DATA), .SELECT_1(P2_SHIP_TL_SEL), .SELECT_2(P1_DOT_TL_SEL), .DATA_2(P1_DOT_TL_DATA),
    .SELECT_0(P2_CUR_TL_SEL), .DATA_0(controlled_buffer_9_out), .OUT_0(out_134), .OUT_1(out_130),
    .OUT_2(out_126), .OUT_3(out_122), .OUT_4(out_118), .OUT_6(out_110), .OUT_7(out_106), .OUT_8(out_102),
    .OUT_9(out_98), .OUT_a(out_94), .OUT_c(out_86), .OUT_12(out_62), .OUT_d(out_82), .OUT_13(out_58),
    .OUT_e(out_78), .OUT_14(out_54), .OUT_f(out_74), .OUT_15(out_50), .OUT_10(out_70), .OUT_16(out_46),
    .OUT_18(out_38), .OUT_19(out_34), .OUT_1a(out_30), .OUT_1b(out_26), .OUT_1c(out_22), .OUT_5(out_114),
    .OUT_b(out_90), .OUT_11(out_66), .OUT_17(out_42), .OUT_1d(out_18));
  not not_5 (not_5_out, PREP_PHASE_END);
  demuxor_30x30x3_main main_18 (
    .DATA_1(P2_SHIP_BL_DATA), .SELECT_1(P2_SHIP_BL_SEL), .SELECT_2(P1_DOT_BL_SEL), .DATA_2(P1_DOT_BL_DATA),
    .SELECT_0(P2_CUR_BL_SEL), .DATA_0(controlled_buffer_10_out), .OUT_0(out_252), .OUT_1(out_248),
    .OUT_2(out_244), .OUT_3(out_240), .OUT_4(out_236), .OUT_6(out_228), .OUT_7(out_224), .OUT_8(out_220),
    .OUT_9(out_216), .OUT_a(out_212), .OUT_c(out_204), .OUT_12(out_180), .OUT_d(out_200), .OUT_13(out_176),
    .OUT_e(out_196), .OUT_14(out_172), .OUT_f(out_192), .OUT_15(out_168), .OUT_10(out_188), .OUT_16(out_164),
    .OUT_18(out_156), .OUT_19(out_152), .OUT_1a(out_148), .OUT_1b(out_144), .OUT_1c(out_140),
    .OUT_5(out_232), .OUT_b(out_208), .OUT_11(out_184), .OUT_17(out_160), .OUT_1d(out_136));
  not not_6 (not_6_out, PREP_PHASE_END);
  demuxor_30x30x3_main main_19 (
    .DATA_1(P1_SHIP_ON_EN_TL_DATA), .SELECT_1(P1_SHIP_ON_EN_TL_SEL), .SELECT_2(P2_DOT_TL_SEL),
    .DATA_2(P2_DOT_TL_DATA), .SELECT_0(P2_CUR_TL_SEL), .DATA_0(controlled_buffer_11_out), .OUT_0(out_372),
    .OUT_1(out_368), .OUT_2(out_364), .OUT_3(out_360), .OUT_4(out_356), .OUT_6(out_348), .OUT_7(out_344),
    .OUT_8(out_340), .OUT_9(out_336), .OUT_a(out_332), .OUT_c(out_324), .OUT_12(out_300), .OUT_d(out_320),
    .OUT_13(out_296), .OUT_e(out_316), .OUT_14(out_292), .OUT_f(out_312), .OUT_15(out_288), .OUT_10(out_308),
    .OUT_16(out_284), .OUT_18(out_276), .OUT_19(out_272), .OUT_1a(out_268), .OUT_1b(out_264),
    .OUT_1c(out_260), .OUT_5(out_352), .OUT_b(out_328), .OUT_11(out_304), .OUT_17(out_280), .OUT_1d(out_256));
  and and_15 (and_15_out, PREP_PHASE_END, CURR_PLAYER);
  demuxor_30x30x3_main main_20 (
    .DATA_1(P1_SHIP_ON_EN_BL_DATA), .SELECT_1(P1_SHIP_ON_EN_BL_SEL), .SELECT_2(P2_DOT_BL_SEL),
    .DATA_2(P2_DOT_BL_DATA), .SELECT_0(P2_CUR_BL_SEL), .DATA_0(controlled_buffer_12_out), .OUT_0(out_492),
    .OUT_1(out_488), .OUT_2(out_484), .OUT_3(out_480), .OUT_4(out_476), .OUT_6(out_468), .OUT_7(out_464),
    .OUT_8(out_460), .OUT_9(out_456), .OUT_a(out_452), .OUT_c(out_444), .OUT_12(out_420), .OUT_d(out_440),
    .OUT_13(out_416), .OUT_e(out_436), .OUT_14(out_412), .OUT_f(out_432), .OUT_15(out_408), .OUT_10(out_428),
    .OUT_16(out_404), .OUT_18(out_396), .OUT_19(out_392), .OUT_1a(out_388), .OUT_1b(out_384),
    .OUT_1c(out_380), .OUT_5(out_472), .OUT_b(out_448), .OUT_11(out_424), .OUT_17(out_400), .OUT_1d(out_376));
  and and_16 (and_16_out, PREP_PHASE_END, CURR_PLAYER);
  assign controlled_buffer_9_out = not_5_out ? P2_CUR_TL_DATA : 30'bz;  // Controlled_Buffer controlled_buffer_9
  assign controlled_buffer_10_out = not_6_out ? P2_CUR_BL_DATA : 30'bz;  // Controlled_Buffer controlled_buffer_10
  assign controlled_buffer_11_out = and_15_out ? P2_CUR_TL_DATA : 30'bz;  // Controlled_Buffer controlled_buffer_11
  assign controlled_buffer_12_out = and_16_out ? P2_CUR_BL_DATA : 30'bz;  // Controlled_Buffer controlled_buffer_12
  not_hit_module_main main_21 (
    .nHIT_X(P1_CUR_X), .nHIT_Y(P1_CUR_Y), .nHIT(and_14_out), .CLK(out_14), .TL_DATA(P1_DOT_TL_DATA),
    .TR_DATA(P1_DOT_TR_DATA), .BL_DATA(P1_DOT_BL_DATA), .BR_DATA(P1_DOT_BR_DATA), .TL_SEL(P1_DOT_TL_SEL),
    .TR_SEL(P1_DOT_TR_SEL), .BL_SEL(P1_DOT_BL_SEL), .BR_SEL(P1_DOT_BR_SEL), .ADDED(P2_DOT_ADDED));
  Multiplexer #(.select(2), .enable("false")) multiplexer_6 (
    .in0(P2_RO_ALIVE[0]), .in1(P2_RO_ALIVE[1]), .in2(P2_RO_ALIVE[2]), .in3(P2_RO_ALIVE[3]),
    .out(P2_CURR_SEG_ALIVE), .sel(P2_SEG_SEL));
  Multiplexer #(.width(3), .enable("false")) multiplexer_7 (
    .in0(3'b010), .in1(3'b001), .out(P2_SHIP_DRAW_SEL), .sel(P2_CURR_SEG_ALIVE));
  Multiplexer #(.width(3), .enable("false")) multiplexer_8 (
    .in0(3'b010), .in1(3'b100), .out(P2_SHIP_DRAW_ON_ENEMY_SEL), .sel(P2_CURR_SEG_ALIVE));
  demuxor_30x30x3_main main_22 (
    .DATA_1(P1_SHIP_ON_EN_BR_DATA), .SELECT_1(P1_SHIP_ON_EN_BR_SEL), .SELECT_2(P2_DOT_BR_SEL),
    .DATA_2(P2_DOT_BR_DATA), .SELECT_0(P2_CUR_BR_SEL), .DATA_0(controlled_buffer_16_out), .OUT_0(out_493),
    .OUT_1(out_489), .OUT_2(out_485), .OUT_3(out_481), .OUT_4(out_477), .OUT_6(out_469), .OUT_7(out_465),
    .OUT_8(out_461), .OUT_9(out_457), .OUT_a(out_453), .OUT_c(out_445), .OUT_12(out_421), .OUT_d(out_441),
    .OUT_13(out_417), .OUT_e(out_437), .OUT_14(out_413), .OUT_f(out_433), .OUT_15(out_409), .OUT_10(out_429),
    .OUT_16(out_405), .OUT_18(out_397), .OUT_19(out_393), .OUT_1a(out_389), .OUT_1b(out_385),
    .OUT_1c(out_381), .OUT_5(out_473), .OUT_b(out_449), .OUT_11(out_425), .OUT_17(out_401), .OUT_1d(out_377));
  demuxor_30x30x3_main main_23 (
    .DATA_1(P2_SHIP_TR_DATA), .SELECT_1(P2_SHIP_TR_SEL), .SELECT_2(P1_DOT_TR_SEL), .DATA_2(P1_DOT_TR_DATA),
    .SELECT_0(P2_CUR_TR_SEL), .DATA_0(controlled_buffer_13_out), .OUT_0(out_135), .OUT_1(out_131),
    .OUT_2(out_127), .OUT_3(out_123), .OUT_4(out_119), .OUT_6(out_111), .OUT_7(out_107), .OUT_8(out_103),
    .OUT_9(out_99), .OUT_a(out_95), .OUT_c(out_87), .OUT_12(out_63), .OUT_d(out_83), .OUT_13(out_59),
    .OUT_e(out_79), .OUT_14(out_55), .OUT_f(out_75), .OUT_15(out_51), .OUT_10(out_71), .OUT_16(out_47),
    .OUT_18(out_39), .OUT_19(out_35), .OUT_1a(out_31), .OUT_1b(out_27), .OUT_1c(out_23), .OUT_5(out_115),
    .OUT_b(out_91), .OUT_11(out_67), .OUT_17(out_43), .OUT_1d(out_19));
  assign controlled_buffer_13_out = not_7_out ? P2_CUR_TR_DATA : 30'bz;  // Controlled_Buffer controlled_buffer_13
  not not_7 (not_7_out, PREP_PHASE_END);
  demuxor_30x30x3_main main_24 (
    .DATA_1(P2_SHIP_BR_DATA), .SELECT_1(P2_SHIP_BR_SEL), .SELECT_2(P1_DOT_BR_SEL), .DATA_2(P1_DOT_BR_DATA),
    .SELECT_0(P2_CUR_BR_SEL), .DATA_0(controlled_buffer_14_out), .OUT_0(out_253), .OUT_1(out_249),
    .OUT_2(out_245), .OUT_3(out_241), .OUT_4(out_237), .OUT_6(out_229), .OUT_7(out_225), .OUT_8(out_221),
    .OUT_9(out_217), .OUT_a(out_213), .OUT_c(out_205), .OUT_12(out_181), .OUT_d(out_201), .OUT_13(out_177),
    .OUT_e(out_197), .OUT_14(out_173), .OUT_f(out_193), .OUT_15(out_169), .OUT_10(out_189), .OUT_16(out_165),
    .OUT_18(out_157), .OUT_19(out_153), .OUT_1a(out_149), .OUT_1b(out_145), .OUT_1c(out_141),
    .OUT_5(out_233), .OUT_b(out_209), .OUT_11(out_185), .OUT_17(out_161), .OUT_1d(out_137));
  assign controlled_buffer_14_out = not_8_out ? P2_CUR_BR_DATA : 30'bz;  // Controlled_Buffer controlled_buffer_14
  not not_8 (not_8_out, PREP_PHASE_END);
  demuxor_30x30x3_main main_25 (
    .DATA_1(P1_SHIP_ON_EN_TR_DATA), .SELECT_1(P1_SHIP_ON_EN_TR_SEL), .SELECT_2(P2_DOT_TR_SEL),
    .DATA_2(P2_DOT_TR_DATA), .SELECT_0(P2_CUR_TR_SEL), .DATA_0(controlled_buffer_15_out), .OUT_0(out_373),
    .OUT_1(out_369), .OUT_2(out_365), .OUT_3(out_361), .OUT_4(out_357), .OUT_6(out_349), .OUT_7(out_345),
    .OUT_8(out_341), .OUT_9(out_337), .OUT_a(out_333), .OUT_c(out_325), .OUT_12(out_301), .OUT_d(out_321),
    .OUT_13(out_297), .OUT_e(out_317), .OUT_14(out_293), .OUT_f(out_313), .OUT_15(out_289), .OUT_10(out_309),
    .OUT_16(out_285), .OUT_18(out_277), .OUT_19(out_273), .OUT_1a(out_269), .OUT_1b(out_265),
    .OUT_1c(out_261), .OUT_5(out_353), .OUT_b(out_329), .OUT_11(out_305), .OUT_17(out_281), .OUT_1d(out_257));
  assign controlled_buffer_15_out = and_17_out ? P2_CUR_TR_DATA : 30'bz;  // Controlled_Buffer controlled_buffer_15
  and and_17 (and_17_out, PREP_PHASE_END, CURR_PLAYER);
  assign controlled_buffer_16_out = and_18_out ? P2_CUR_BR_DATA : 30'bz;  // Controlled_Buffer controlled_buffer_16
  and and_18 (and_18_out, PREP_PHASE_END, CURR_PLAYER);
  Comparator #(.width(4), .mode("unsigned")) comparator_6 (
    .a(P2_CURR_SHIP_ADD), .b(4'b0000), .gt(comparator_6_gt));  // open: eq, lt
  ship_xyr_to_screen_xy_main main_26 (
    .in_1(P2_RO_SHIP_X), .in_2(P2_RO_SHIP_Y), .in_3(P2_RO_ROTATED), .OUT_X_00(main_26_out_x_00),
    .OUT_Y_00(main_26_out_y_00), .OUT_X_01(main_26_out_x_01), .OUT_Y_01(main_26_out_y_01),
    .OUT_X_10(main_26_out_x_10), .OUT_Y_10(main_26_out_y_10), .OUT_X_11(main_26_out_x_11),
    .OUT_Y_11(main_26_out_y_11));
  screen_xy_to_screen_data_main main_27 (
    .SCREEN_X(P2_SHIP_SCR_X), .SCREEN_Y(P2_SHIP_SCR_Y), .DATA_TO_DISPLAY(P2_SHIP_DRAW_SEL),
    .TL_SEL_OUT(P2_SHIP_TL_SEL), .TR_SEL_OUT(P2_SHIP_TR_SEL), .BL_SEL_OUT(P2_SHIP_BL_SEL),
    .BR_SEL_OUT(P2_SHIP_BR_SEL), .TL_DATA_OUT(P2_SHIP_TL_DATA), .TR_DATA_OUT(P2_SHIP_TR_DATA),
    .BL_DATA_OUT(P2_SHIP_BL_DATA), .BR_DATA_OUT(P2_SHIP_BR_DATA), .CLK(out_14), .ENABLE(and_19_out));
  and and_19 (and_19_out, P2_SHIP_DRAW_ENABLE, comparator_6_gt);
  screen_xy_to_screen_data_main main_28 (
    .SCREEN_X(P2_SHIP_SCR_X), .SCREEN_Y(P2_SHIP_SCR_Y), .DATA_TO_DISPLAY(P2_SHIP_DRAW_ON_ENEMY_SEL),
    .TL_SEL_OUT(P2_SHIP_ON_EN_TL_SEL), .TR_SEL_OUT(P2_SHIP_ON_EN_TR_SEL), .BL_SEL_OUT(P2_SHIP_ON_EN_BL_SEL),
    .BR_SEL_OUT(P2_SHIP_ON_EN_BR_SEL), .TL_DATA_OUT(P2_SHIP_ON_EN_TL_DATA),
    .TR_DATA_OUT(P2_SHIP_ON_EN_TR_DATA), .BL_DATA_OUT(P2_SHIP_ON_EN_BL_DATA),
    .BR_DATA_OUT(P2_SHIP_ON_EN_BR_DATA), .CLK(out_14), .ENABLE(and_20_out));
  and and_20 (and_20_out, P2_SHIP_DRAW_ENABLE, comparator_7_gt);
  Comparator #(.width(4), .mode("unsigned")) comparator_7 (
    .a(P2_CURR_SHIP_ADD), .b(4'b0000), .gt(comparator_7_gt));  // open: eq, lt
  and and_21 (P2_ADD_SHIP, P2_CONF, ~PREP_PHASE_END);  // AND_Gate
  and and_22 (P2_CHECK_SHIP, P2_CONF, PREP_PHASE_END);
  Comparator #(.width(2), .mode("unsigned")) comparator_8 (
    .a(P2_SEG_SEL), .b(P2_RO_SHIP_TYPE), .eq(comparator_8_eq), .lt(comparator_8_lt));  // open: gt
  or or_4 (P2_SHIP_DRAW_ENABLE, comparator_8_eq, comparator_8_lt);
  Multiplexer #(.select(2), .width(6), .enable("false")) multiplexer_9 (
    .in0(main_26_out_x_00), .in1(main_26_out_x_01), .in2(main_26_out_x_10), .in3(main_26_out_x_11),
    .out(P2_SHIP_SCR_X), .sel(P2_SEG_SEL));
  Multiplexer #(.select(2), .width(6), .enable("false")) multiplexer_10 (
    .in0(main_26_out_y_00), .in1(main_26_out_y_01), .in2(main_26_out_y_10), .in3(main_26_out_y_11),
    .out(P2_SHIP_SCR_Y), .sel(P2_SEG_SEL));
  cursor_module_main main_29 (
    .CUR_X(main_29_cur_x), .CLK(out_14), .KEYBOARD_OUT(in_5), .KEYBOARD_RST(in_4), .TL_SEL(main_29_tl_sel),
    .TR_SEL(main_29_tr_sel), .BL_SEL(main_29_bl_sel), .BR_SEL(main_29_br_sel), .TL_DATA(main_29_tl_data),
    .TR_DATA(main_29_tr_data), .BL_DATA(main_29_bl_data), .BR_DATA(main_29_br_data),
    .CONFIRM(main_29_confirm), .CUR_Y(main_29_cur_y), .ROTATED(main_29_rotated));
  bots_main main_30 (
    .CURR_PLAYER(CURR_PLAYER), .PREP_PHASE_END(PREP_PHASE_END), .CLR(1'b0), .CLK(out_14), .X(main_30_x),
    .Y(main_30_y), .ROTATED(main_30_rotated), .CONFIRM(main_30_confirm), .SHIPS_NUMBER(P2_CURR_SHIP_ADD),
    .WIN(P2_HIT), .HIT(P2_WIN), .CHECKING(P2_CHECKING));
  and and_23 (and_23_out, ~PREP_PHASE_END, main_29_confirm);  // AND_Gate
  and and_24 (and_24_out, main_29_confirm, CURR_PLAYER);
  assign P2_CUR_X = 1'b0 ? main_29_cur_x : 4'bz;  // Controlled_Buffer controlled_buffer_17
  assign P2_CUR_Y = 1'b0 ? main_29_cur_y : 4'bz;  // Controlled_Buffer controlled_buffer_18
  assign P2_ROTATED = 1'b0 ? main_29_rotated : 1'bz;  // Controlled_Buffer controlled_buffer_19
  Pull_Resistor pull_resistor_1 (.node(P2_CONF));
  or or_5 (or_5_out, and_23_out, and_24_out);
  assign P2_CONF = 1'b0 ? or_5_out : 1'bz;  // Controlled_Buffer controlled_buffer_20
  assign P2_CUR_TL_SEL = 1'b0 ? main_29_tl_sel : 5'bz;  // Controlled_Buffer controlled_buffer_21
  assign P2_CUR_TR_SEL = 1'b0 ? main_29_tr_sel : 5'bz;  // Controlled_Buffer controlled_buffer_22
  assign P2_CUR_BL_SEL = 1'b0 ? main_29_bl_sel : 5'bz;  // Controlled_Buffer controlled_buffer_23
  assign P2_CUR_BR_SEL = 1'b0 ? main_29_br_sel : 5'bz;  // Controlled_Buffer controlled_buffer_24
  assign P2_CUR_TL_DATA = 1'b0 ? main_29_tl_data : 30'bz;  // Controlled_Buffer controlled_buffer_25
  assign P2_CUR_TR_DATA = 1'b0 ? main_29_tr_data : 30'bz;  // Controlled_Buffer controlled_buffer_26
  assign P2_CUR_BL_DATA = 1'b0 ? main_29_bl_data : 30'bz;  // Controlled_Buffer controlled_buffer_27
  assign P2_CUR_BR_DATA = 1'b0 ? main_29_br_data : 30'bz;  // Controlled_Buffer controlled_buffer_28
  not not_9 (not_9_out, 1'b0);
  assign P2_CUR_X = not_9_out ? main_30_x : 4'bz;  // Controlled_Buffer controlled_buffer_29
  assign P2_CUR_Y = not_9_out ? main_30_y : 4'bz;  // Controlled_Buffer controlled_buffer_30
  assign P2_ROTATED = not_9_out ? main_30_rotated : 1'bz;  // Controlled_Buffer controlled_buffer_31
  assign P2_CONF = not_9_out ? main_30_confirm : 1'bz;  // Controlled_Buffer controlled_buffer_32

  assign out_15 = out_14;

  // Other names for the same wires on the sheet: CLK = out_14

  // Notes on the sheet:
  //   sunk
  //   alive
  //   sunk
  //   none
  //   1 jak gracze wybiora statki juz
  //   sunk
  //   alive
  //   sunk
  //   none
endmodule
