// Logisim project arrow.circ as structural Verilog: 1 circuit, main circuit main
module main (
  input  in_1
);

  wire [4:0] multiplexer_1_out_2, multiplexer_1_out_3, multiplexer_1_out_4;
  wire [14:0] multiplexer_1_out;

  DotMatrix #(.matrixcols(8), .matrixrows(5)) dotmatrix_1 (
    .col0({5{1'b0}}), .col1(multiplexer_1_out_4), .col2(multiplexer_1_out_3), .col3(multiplexer_1_out_2),
    .col4(multiplexer_1_out[14:10]), .col5(multiplexer_1_out[9:5]), .col6(multiplexer_1_out[4:0]),
    .col7({5{1'b0}}));
  Multiplexer #(.width(30), .enable("false")) multiplexer_1 (
    .in0(30'h8ef9084), .in1(30'h8427dc4),
    .out({multiplexer_1_out_4, multiplexer_1_out_3, multiplexer_1_out_2, multiplexer_1_out}), .sel(in_1));
endmodule
