// Logisim project game.circ as structural Verilog: 1 circuit, main circuit main
module main (
);

  wire K1CLK, K1RST, K2CLK, K2RST;
  wire [6:0] K1DATA, K2DATA;

  // app_main main_1: pin names not known
  DotMatrix #(.matrixcols(30), .matrixrows(30), .persist(500)) dotmatrix_1 ();  // open: col0, col1, col2, col3, col4, col5, col6, col7, col8, col9, col10, col11, col12, col13, col14, col15, col16, col17, col18, col19, col20, col21, col22, col23, col24, col25, col26, col27, col28, col29
  DotMatrix #(.matrixcols(30), .matrixrows(30), .persist(500)) dotmatrix_2 ();  // open: col0, col1, col2, col3, col4, col5, col6, col7, col8, col9, col10, col11, col12, col13, col14, col15, col16, col17, col18, col19, col20, col21, col22, col23, col24, col25, col26, col27, col28, col29
  DotMatrix #(.matrixcols(30), .matrixrows(30), .persist(500)) dotmatrix_3 ();  // open: col0, col1, col2, col3, col4, col5, col6, col7, col8, col9, col10, col11, col12, col13, col14, col15, col16, col17, col18, col19, col20, col21, col22, col23, col24, col25, col26, col27, col28, col29
  DotMatrix #(.matrixcols(30), .matrixrows(30), .persist(500)) dotmatrix_4 ();  // open: col0, col1, col2, col3, col4, col5, col6, col7, col8, col9, col10, col11, col12, col13, col14, col15, col16, col17, col18, col19, col20, col21, col22, col23, col24, col25, col26, col27, col28, col29
  DotMatrix #(.matrixcols(30), .matrixrows(30), .persist(500)) dotmatrix_5 ();  // open: col0, col1, col2, col3, col4, col5, col6, col7, col8, col9, col10, col11, col12, col13, col14, col15, col16, col17, col18, col19, col20, col21, col22, col23, col24, col25, col26, col27, col28, col29
  DotMatrix #(.matrixcols(30), .matrixrows(30), .persist(500)) dotmatrix_6 ();  // open: col0, col1, col2, col3, col4, col5, col6, col7, col8, col9, col10, col11, col12, col13, col14, col15, col16, col17, col18, col19, col20, col21, col22, col23, col24, col25, col26, col27, col28, col29
  DotMatrix #(.matrixcols(30), .matrixrows(30), .persist(500)) dotmatrix_7 ();  // open: col0, col1, col2, col3, col4, col5, col6, col7, col8, col9, col10, col11, col12, col13, col14, col15, col16, col17, col18, col19, col20, col21, col22, col23, col24, col25, col26, col27, col28, col29
  DotMatrix #(.matrixcols(30), .matrixrows(30), .persist(500)) dotmatrix_8 ();  // open: col0, col1, col2, col3, col4, col5, col6, col7, col8, col9, col10, col11, col12, col13, col14, col15, col16, col17, col18, col19, col20, col21, col22, col23, col24, col25, col26, col27, col28, col29
  DotMatrix #(.matrixcols(30), .matrixrows(30), .persist(500)) dotmatrix_9 ();  // open: col0, col1, col2, col3, col4, col5, col6, col7, col8, col9, col10, col11, col12, col13, col14, col15, col16, col17, col18, col19, col20, col21, col22, col23, col24, col25, col26, col27, col28, col29
  DotMatrix #(.matrixcols(30), .matrixrows(30), .persist(500)) dotmatrix_10 ();  // open: col0, col1, col2, col3, col4, col5, col6, col7, col8, col9, col10, col11, col12, col13, col14, col15, col16, col17, col18, col19, col20, col21, col22, col23, col24, col25, col26, col27, col28, col29
  DotMatrix #(.matrixcols(8), .matrixrows(5)) dotmatrix_11 ();  // open: col0, col1, col2, col3, col4, col5, col6, col7
  DotMatrix #(.matrixcols(30), .matrixrows(30), .persist(500)) dotmatrix_12 ();  // open: col0, col1, col2, col3, col4, col5, col6, col7, col8, col9, col10, col11, col12, col13, col14, col15, col16, col17, col18, col19, col20, col21, col22, col23, col24, col25, col26, col27, col28, col29
  DotMatrix #(.matrixcols(30), .matrixrows(30), .persist(500)) dotmatrix_13 ();  // open: col0, col1, col2, col3, col4, col5, col6, col7, col8, col9, col10, col11, col12, col13, col14, col15, col16, col17, col18, col19, col20, col21, col22, col23, col24, col25, col26, col27, col28, col29
  DotMatrix #(.matrixcols(30), .matrixrows(30), .persist(500)) dotmatrix_14 ();  // open: col0, col1, col2, col3, col4, col5, col6, col7, col8, col9, col10, col11, col12, col13, col14, col15, col16, col17, col18, col19, col20, col21, col22, col23, col24, col25, col26, col27, col28, col29
  DotMatrix #(.matrixcols(30), .matrixrows(30), .persist(500)) dotmatrix_15 ();  // open: col0, col1, col2, col3, col4, col5, col6, col7, col8, col9, col10, col11, col12, col13, col14, col15, col16, col17, col18, col19, col20, col21, col22, col23, col24, col25, col26, col27, col28, col29
  DotMatrix #(.matrixcols(30), .matrixrows(30), .persist(500)) dotmatrix_16 ();  // open: col0, col1, col2, col3, col4, col5, col6, col7, col8, col9, col10, col11, col12, col13, col14, col15, col16, col17, col18, col19, col20, col21, col22, col23, col24, col25, col26, col27, col28, col29
  DotMatrix #(.matrixcols(30), .matrixrows(30), .persist(500)) dotmatrix_17 ();  // open: col0, col1, col2, col3, col4, col5, col6, col7, col8, col9, col10, col11, col12, col13, col14, col15, col16, col17, col18, col19, col20, col21, col22, col23, col24, col25, col26, col27, col28, col29
  Keyboard keyboard_1 (.clk(K1CLK), .clr(K1RST), .data(K1DATA));  // open: re, avail
  Keyboard keyboard_2 (.clk(K2CLK), .clr(K2RST), .data(K2DATA));  // open: re, avail
endmodule
