// Logisim project not_hit_module.circ as structural Verilog: 1 circuit, main circuit main
module main (
  input  [3:0] nHIT_X,
  input  [3:0] nHIT_Y,
  input  nHIT,
  input  CLK,
  output [29:0] TL_DATA,
  output [29:0] TR_DATA,
  output [29:0] BL_DATA,
  output [29:0] BR_DATA,
  output [4:0] TL_SEL,
  output [4:0] TR_SEL,
  output [4:0] BL_SEL,
  output [4:0] BR_SEL
);

  wire CLK_5, main_1_p8, not_1_out;
  wire [3:0] main_1_p6, main_1_p7;
  wire [5:0] main_2_out_x_00, main_2_out_y_00;

  // not_hit_ram_storage_main main_1: pin names not known; wires that end beside it: nHIT_X, nHIT_Y, nHIT, 1'b0, CLK_5, main_1_p6, main_1_p7, main_1_p8
  Counter #(.width(4), .max('h5)) counter_1 (.carry(CLK_5), .clk(CLK));  // open: load, D, count, Q, clr
  ship_xyr_to_screen_xy_main main_2 (
    .INPUT(main_1_p6), .in_2(main_1_p7), .CONST(1'b0), .OUT_X_00(main_2_out_x_00), .OUT_Y_00(main_2_out_y_00));  // open: OUT_X_01, OUT_Y_01, OUT_X_10, OUT_Y_10, OUT_X_11, OUT_Y_11
  not not_1 (not_1_out, main_1_p8);
  screen_xy_to_screen_data_main main_3 (
    .SCREEN_X(main_2_out_x_00), .SCREEN_Y(main_2_out_y_00), .DATA_TO_DISPLAY(3'b011), .TL_SEL_OUT(TL_SEL),
    .TR_SEL_OUT(TR_SEL), .BL_SEL_OUT(BL_SEL), .BR_SEL_OUT(BR_SEL), .TL_DATA_OUT(TL_DATA),
    .TR_DATA_OUT(TR_DATA), .BL_DATA_OUT(BL_DATA), .BR_DATA_OUT(BR_DATA), .CLK(CLK), .ENABLE(not_1_out));
endmodule
