// Logisim project not_hit_ram_storage.circ as structural Verilog: 1 circuit, main circuit main
module main (
  input  IF_1__save_input,
  input  CLR,
  input  [3:0] X,
  input  [3:0] Y,
  input  CLK,
  output [3:0] X_2,
  output [3:0] Y_2,
  output [7:0] out_8,
  output [7:0] out_9
);

  wire CLK_t, comparator_1_eq, comparator_2_lt, controlled_buffer_1_out, controlled_buffer_2_out,
       main_2_out_3, MEM_END, not_1_out, not_2_out, not_hit___0, not_hit___1, or_1_out, SAVE_N_DATA, STORE;
  wire [7:0] ADDRESS, STABLE_COUNTER_q;

  Clock clock_1 (.out(CLK_t));
  Register register_1 (.D({Y, X}), .Q(out_8), .clk(IF_1__save_input), .clr(CLR));  // open: en
  not not_1 (not_1_out, not_hit___0);
  assign controlled_buffer_1_out = not_1_out ? IF_1__save_input : 1'bz;  // Controlled_Buffer controlled_buffer_1
  Pull_Resistor pull_resistor_1 (.node(controlled_buffer_1_out));
  tick_main main_1 (.in_1(CLK_t), .in_2(controlled_buffer_1_out), .out_3(SAVE_N_DATA));
  Comparator comparator_1 (.a(out_8), .b(out_9), .eq(comparator_1_eq));  // open: gt, lt
  Counter #(.width(2), .max('h2), .ongoal("stay")) count_form_0 (
    .carry(not_hit___1), .clk(SAVE_N_DATA), .clr(CLR));  // open: load, D, count, Q
  Counter #(.width(1), .max('h1), .ongoal("stay")) count_form_0_2 (
    .carry(not_hit___0), .clk(SAVE_N_DATA), .clr(CLR));  // open: load, D, count, Q
  Pull_Resistor pull_resistor_2 (.node(SAVE_N_DATA));
  Counter #(.width(2), .max('h2), .ongoal("stay")) count_form_0_3 (
    .clk(STORE), .clr(STORE));  // open: load, D, count, Q, carry
  Counter #(.max('h90)) STABLE_COUNTER (
    .Q(STABLE_COUNTER_q), .clk(controlled_buffer_2_out), .clr(CLR));  // open: load, D, count, carry
  assign controlled_buffer_2_out = not_hit___0 ? SAVE_N_DATA : 1'bz;  // Controlled_Buffer controlled_buffer_2
  Comparator comparator_2 (.a(STABLE_COUNTER_q), .b(ADDRESS), .eq(MEM_END), .lt(comparator_2_lt));  // open: gt
  RAM #(.bus("separate")) ram_1 (
    .addr(ADDRESS), .din(out_8), .data(out_9), .str(STORE), .clk(CLK_t), .ld(1'b1), .clr(CLR));  // open: sel
  not not_2 (not_2_out, not_hit___0);
  Pull_Resistor pull_resistor_3 (.node(STORE));
  assign STORE = not_2_out ? MEM_END : 1'bz;  // Controlled_Buffer controlled_buffer_3
  assign {Y_2, X_2} = not_hit___0 ? out_9 : 8'bz;  // Controlled_Buffer controlled_buffer_4
  tick_main main_2 (.in_1(CLK_t), .in_2(MEM_END), .out_3(main_2_out_3));
  or or_1 (or_1_out, main_2_out_3, comparator_2_lt, IF_1__save_input, CLR, SAVE_N_DATA);
  Counter #(.max('h90)) UNSTABLE_COUNTER (.Q(ADDRESS), .clk(CLK_t), .clr(or_1_out));  // open: load, D, count, carry

  // Other names for the same wires on the sheet: CURRENT_MEM_OUT[7:0] = out_9; DATA_TO_CHECK[7:0] = out_8;
  //   nHIT = IF_1__save_input

  // Notes on the sheet:
  //   FITRST DATA SAVER
endmodule
